# Fritzing sketch Fritzing (saved by Fritzing 0.9.3b)
circuit board: 8.46667cm x 5.64444cm
breadboards: 1

parts:
  WeMos_D1_Mini1 = WeMos D1 Mini
  U1 = X9015 [package=so08]
  R2 = Resistor [tolerance=±1% resistance=320 package=THT]
  R1 = Resistor [tolerance=±1% resistance=1k package=THT]
  J1 = female pin header, 3 pins [form="♀ (female)"]

nets:
  3.3V: WeMos_D1_Mini1.3V3, U1.RH_VH, U1.VCC, R1.Pin_1
  5V: WeMos_D1_Mini1.5V, J1.pin2
  N1: WeMos_D1_Mini1.D2, U1.U_D_
  N2: WeMos_D1_Mini1.D3, U1.INC_
  GND: WeMos_D1_Mini1.G, U1.VSS, U1.CS_, R2.Pin_0, J1.pin3
  N3: U1.RW_VW, J1.pin1
  N4: U1.RL_VL, R2.Pin_1, R1.Pin_0
